// Logisim project Cravo_project.circ as structural Verilog: 5 circuits, main circuit ADD_4
module ADD_4 (
  input  [3:0] in_1,
  input  [3:0] in_2,
  input  in_3,
  output out_4,
  output [3:0] out_5
);

  wire add_1_2_carryout, add_1_3_carryout, add_1_4_carryout;

  ADD_1 add_1_1 (.A(in_2[3]), .B(in_1[3]), .CarryON(add_1_2_carryout), .S(out_5[3]), .CarryOUT(out_4));
  ADD_1 add_1_2 (.A(in_2[2]), .B(in_1[2]), .CarryON(add_1_3_carryout), .S(out_5[2]), .CarryOUT(add_1_2_carryout));
  ADD_1 add_1_3 (.A(in_2[1]), .B(in_1[1]), .CarryON(add_1_4_carryout), .S(out_5[1]), .CarryOUT(add_1_3_carryout));
  ADD_1 add_1_4 (.A(in_2[0]), .B(in_1[0]), .CarryON(in_3), .S(out_5[0]), .CarryOUT(add_1_4_carryout));
endmodule

module ADD_1 (
  input  A,
  input  B,
  input  CarryON,
  output S,
  output CarryOUT
);

  wire and_1_out, and_2_out, or_1_out, xor_1_out;

  xor xor_1 (xor_1_out, A, B);
  or or_1 (or_1_out, CarryON, B);
  and and_1 (and_1_out, CarryON, B);
  LED led_1 (.in(S));
  xor xor_2 (S, xor_1_out, CarryON);
  and and_2 (and_2_out, or_1_out, A);
  LED led_2 (.in(CarryOUT));
  or or_2 (CarryOUT, and_2_out, and_1_out);
endmodule

module Main (
  input  [3:0] in_1,
  input  [3:0] in_2,
  output out_3,
  output out_4,
  output [3:0] out_5,
  output [3:0] out_6
);

  ADD_4 add_4_1 (.out_4(out_3), .in_3(1'b0), .out_5(out_5), .in_2(in_1), .in_1(in_2));
  SUB_4 sub_4_1 (.out_4(out_4), .in_3(1'b0), .out_5(out_6), .in_2(in_1), .in_1(in_2));
endmodule

module SUB_1 (
  input  A,
  input  B,
  input  CarryON,
  output S,
  output CarryOUT
);

  wire and_1_out, and_2_out, or_1_out, xor_1_out;

  xor xor_1 (xor_1_out, A, B);
  or or_1 (or_1_out, CarryON, B);
  and and_1 (and_1_out, or_1_out, ~A);  // AND_Gate
  and and_2 (and_2_out, CarryON, B);
  LED led_1 (.in(S));
  xor xor_2 (S, xor_1_out, CarryON);
  LED led_2 (.in(CarryOUT));
  or or_2 (CarryOUT, and_1_out, and_2_out);
endmodule

module SUB_4 (
  input  [3:0] in_1,
  input  [3:0] in_2,
  input  in_3,
  output out_4,
  output [3:0] out_5
);

  wire sub_1_2_carryout, sub_1_3_carryout, sub_1_4_carryout;

  SUB_1 sub_1_1 (.A(in_2[3]), .B(in_1[3]), .CarryON(sub_1_2_carryout), .S(out_5[3]), .CarryOUT(out_4));
  SUB_1 sub_1_2 (.A(in_2[2]), .B(in_1[2]), .CarryON(sub_1_3_carryout), .S(out_5[2]), .CarryOUT(sub_1_2_carryout));
  SUB_1 sub_1_3 (.A(in_2[1]), .B(in_1[1]), .CarryON(sub_1_4_carryout), .S(out_5[1]), .CarryOUT(sub_1_3_carryout));
  SUB_1 sub_1_4 (.A(in_2[0]), .B(in_1[0]), .CarryON(in_3), .S(out_5[0]), .CarryOUT(sub_1_4_carryout));
endmodule
